# Fritzing sketch ArduinoAntennaSwitch - Relay (saved by Fritzing 0.9.2b)
breadboards: 1

parts:
  Q1 = TRANSISTOR_NPN [package=to-92-ammo]
  R1 = Resistor [tolerance=±5% resistance=220 package=THT]
  U1 = RELAY-2 [package=relay-g5v]

nets:
  N1: Q1.E, U1.6, U1.9, U1.10
  N2: Q1.B, R1.Pin_1

notes:
  To Decoder
  5V DC
  Ground
  Antenna- Coax Shield
